// Logisim project proutiti.circ as structural Verilog: 3 circuits, main circuit main
module main (
  input  [7:0] A,
  input  [7:0] B,
  output [3:0] P
);

  and and_1 (P[0], A[0], B[0]);
endmodule

module HaAdd (
  input  A,
  input  B,
  output S,
  output R
);

  xor xor_1 (S, A, B);
  and and_1 (R, A, B);
endmodule

module FuAdd (
  input  A,
  input  B,
  input  R,
  output S,
  output Res
);

  wire haadd_1_r, haadd_1_s, haadd_2_r;

  HaAdd haadd_1 (.A(B), .B(R), .S(haadd_1_s), .R(haadd_1_r));
  HaAdd haadd_2 (.A(A), .B(haadd_1_s), .S(S), .R(haadd_2_r));
  or or_1 (Res, haadd_2_r, haadd_1_r);
endmodule
